// Logisim project lab5_final_circuit.circ as structural Verilog: 13 circuits, main circuit one_bit_adder
module one_bit_adder (
  input  A,
  input  B,
  input  Cin,
  output S,
  output Cout
);

  wire and_1_out, and_2_out, xor_1_out;

  xor xor_1 (xor_1_out, A, B);
  xor xor_2 (S, xor_1_out, Cin);
  and and_1 (and_1_out, xor_1_out, Cin);
  and and_2 (and_2_out, A, B);
  or or_1 (Cout, and_1_out, and_2_out);
endmodule

module one_bit_Alu (
  input  [3:0] ALU_ctrl,
  input  A,
  input  B,
  input  C_in,
  output R,
  output C_out
);

  wire and_1_out, multiplexer_1_out, not_1_out, one_bit_adder_1_s, or_1_out, xor_1_out;

  not not_1 (not_1_out, B);
  Multiplexer #(.enable("false")) multiplexer_1 (.in0(B), .in1(not_1_out), .out(multiplexer_1_out), .sel(ALU_ctrl[2]));
  and and_1 (and_1_out, A, multiplexer_1_out);
  or or_1 (or_1_out, A, multiplexer_1_out);
  xor xor_1 (xor_1_out, A, multiplexer_1_out);
  one_bit_adder one_bit_adder_1 (.A(A), .B(multiplexer_1_out), .Cin(C_in), .S(one_bit_adder_1_s), .Cout(C_out));
  Multiplexer #(.enable("false"), .select(2)) multiplexer_2 (
    .in0(and_1_out), .in1(or_1_out), .in2(xor_1_out), .in3(one_bit_adder_1_s), .out(R), .sel(ALU_ctrl[1:0]));
endmodule

module four_bit_alu (
  input  C_in,
  input  [3:0] ALU_Ctrl,
  input  [3:0] A,
  input  [3:0] B,
  output [3:0] Result,
  output O
);

  wire one_bit_alu_1_c_out, one_bit_alu_2_c_out, one_bit_alu_3_c_out;

  one_bit_Alu one_bit_alu_1 (
    .ALU_ctrl(ALU_Ctrl), .A(A[0]), .B(B[0]), .C_in(C_in), .R(Result[0]), .C_out(one_bit_alu_1_c_out));
  one_bit_Alu one_bit_alu_2 (
    .ALU_ctrl(ALU_Ctrl), .A(A[1]), .B(B[1]), .C_in(one_bit_alu_1_c_out), .R(Result[1]),
    .C_out(one_bit_alu_2_c_out));
  one_bit_Alu one_bit_alu_3 (
    .ALU_ctrl(ALU_Ctrl), .A(A[2]), .B(B[2]), .C_in(one_bit_alu_2_c_out), .R(Result[2]),
    .C_out(one_bit_alu_3_c_out));
  one_bit_Alu _1_bit_ALU (
    .ALU_ctrl(ALU_Ctrl), .A(A[3]), .B(B[3]), .C_in(one_bit_alu_3_c_out), .R(Result[3]), .C_out(O));
endmodule

module thirtytwo_bit_ALU (
  input  [3:0] ALU_Ctrl,
  input  [31:0] A,
  input  [31:0] B,
  output [31:0] Result,
  output C_out
);

  wire four_bit_alu_1_o, four_bit_alu_2_o, four_bit_alu_3_o, four_bit_alu_4_o, four_bit_alu_5_o,
       four_bit_alu_6_o, four_bit_alu_7_o;

  four_bit_alu four_bit_alu_1 (
    .C_in(ALU_Ctrl[2]), .ALU_Ctrl(ALU_Ctrl), .A(A[3:0]), .B(B[3:0]), .Result(Result[3:0]),
    .O(four_bit_alu_1_o));
  four_bit_alu four_bit_alu_2 (
    .C_in(four_bit_alu_1_o), .ALU_Ctrl(ALU_Ctrl), .A(A[7:4]), .B(B[7:4]), .Result(Result[7:4]),
    .O(four_bit_alu_2_o));
  four_bit_alu four_bit_alu_3 (
    .C_in(four_bit_alu_2_o), .ALU_Ctrl(ALU_Ctrl), .A(A[11:8]), .B(B[11:8]), .Result(Result[11:8]),
    .O(four_bit_alu_3_o));
  four_bit_alu four_bit_alu_4 (
    .C_in(four_bit_alu_3_o), .ALU_Ctrl(ALU_Ctrl), .A(A[15:12]), .B(B[15:12]), .Result(Result[15:12]),
    .O(four_bit_alu_4_o));
  four_bit_alu four_bit_alu_5 (
    .C_in(four_bit_alu_4_o), .ALU_Ctrl(ALU_Ctrl), .A(A[19:16]), .B(B[19:16]), .Result(Result[19:16]),
    .O(four_bit_alu_5_o));
  four_bit_alu four_bit_alu_6 (
    .C_in(four_bit_alu_5_o), .ALU_Ctrl(ALU_Ctrl), .A(A[23:20]), .B(B[23:20]), .Result(Result[23:20]),
    .O(four_bit_alu_6_o));
  four_bit_alu four_bit_alu_7 (
    .C_in(four_bit_alu_6_o), .ALU_Ctrl(ALU_Ctrl), .A(A[27:24]), .B(B[27:24]), .Result(Result[27:24]),
    .O(four_bit_alu_7_o));
  four_bit_alu four_bit_alu_8 (
    .C_in(four_bit_alu_7_o), .ALU_Ctrl(ALU_Ctrl), .A(A[31:28]), .B(B[31:28]), .Result(Result[31:28]),
    .O(C_out));
endmodule

module ALU_Ctrl (
  input  I30,
  input  I14,
  input  I13,
  input  I12,
  input  I6,
  input  I5,
  input  I4,
  output ALU_Ctrl3,
  output ALU_Ctrl2,
  output ALU_Ctrl1,
  output ALU_Ctrl0,
  output ALU_Src
);

  wire and_2_out, not_1_out, not_2_out, not_3_out, not_4_out, not_5_out;

  not not_1 (not_1_out, I14);
  not not_2 (not_2_out, I13);
  not not_3 (not_3_out, I12);
  not not_4 (not_4_out, I5);
  not not_5 (not_5_out, I4);
  and and_1 (ALU_Ctrl2, I30, not_2_out, I5);
  or or_1 (ALU_Ctrl1, not_2_out, not_5_out);
  and and_2 (and_2_out, I13, not_3_out);
  or or_2 (ALU_Src, not_4_out, not_5_out);
  or or_3 (ALU_Ctrl0, not_1_out, and_2_out);

  assign ALU_Ctrl3 = 1'b0;
endmodule

module ImmGen (
  input  [31:0] Instruction,
  output [31:0] IMM32
);

  Multiplexer #(.enable("false"), .width(4)) multiplexer_1 (
    .in0(Instruction[24:21]), .in1(Instruction[11:8]), .out(IMM32[4:1]), .sel(Instruction[5]));
  Multiplexer #(.enable("false")) multiplexer_2 (
    .in0(Instruction[31]), .in1(Instruction[7]), .out(IMM32[11]), .sel(Instruction[6]));
  Multiplexer #(.enable("false"), .select(2)) multiplexer_3 (
    .in0(Instruction[20]), .in1(Instruction[7]), .in3(1'b0), .out(IMM32[0]), .sel(Instruction[6:5]));  // open: in2
  assign IMM32[31:12] = {{19{Instruction[31]}}, Instruction[31]};  // Bit_Extender bit_extender_1

  assign IMM32[10:5] = Instruction[30:25];

  // Other names for the same wires on the sheet: I30_25[5:0] = Instruction[30:25]; I5 = Instruction[5];
  //   I6_5[1:0] = Instruction[6:5]; I6 = Instruction[6]; I7 = Instruction[7]; I11_8[3:0] = Instruction[11:8];
  //   I20 = Instruction[20]; I24_21[3:0] = Instruction[24:21]; I31 = Instruction[31]
endmodule

module thirtytwo_register_file (
  input  Clock_in,
  input  Write,
  input  [4:0] WReg,
  input  [31:0] WData,
  input  [4:0] RReg1,
  input  [4:0] RReg2,
  output [31:0] RData1,
  output [31:0] RData2
);

  wire I0, I1, I2, I3, I4, I5, I6, I7, I8, I9, I10, I11, I12, I13, I14, I15, I16, I17, I18, I19, I20, I21,
       I22, I23, I24, I25, I26, I27, I28, I29, I30, I31;
  wire [31:0] B0, B1, B2, B3, B4, B5, B6, B7, B8, B9, B10, B11, B12, B13, B14, B15, B16, B17, B18, B19, B20,
       B21, B22, B23, B24, B25, B26, B27, B28, B29, B30, B31;

  Register #(.width(32)) register_1 (.D(WData), .en(I0), .clk(Clock_in), .Q(B0), .clr(Write));
  Register #(.width(32)) register_2 (.D(WData), .en(I1), .clk(Clock_in), .Q(B1));  // open: clr
  Register #(.width(32)) register_3 (.D(WData), .en(I2), .clk(Clock_in), .Q(B2));  // open: clr
  Register #(.width(32)) register_4 (.D(WData), .en(I3), .clk(Clock_in), .Q(B3));  // open: clr
  Register #(.width(32)) register_5 (.D(WData), .en(I4), .clk(Clock_in), .Q(B4));  // open: clr
  Register #(.width(32)) register_6 (.D(WData), .en(I5), .clk(Clock_in), .Q(B5));  // open: clr
  Register #(.width(32)) register_7 (.D(WData), .en(I6), .clk(Clock_in), .Q(B6));  // open: clr
  Register #(.width(32)) register_8 (.D(WData), .en(I7), .clk(Clock_in), .Q(B7));  // open: clr
  Register #(.width(32)) register_9 (.D(WData), .en(I8), .clk(Clock_in), .Q(B8));  // open: clr
  Register #(.width(32)) register_10 (.D(WData), .en(I9), .clk(Clock_in), .Q(B9));  // open: clr
  Register #(.width(32)) register_11 (.D(WData), .en(I10), .clk(Clock_in), .Q(B10));  // open: clr
  Register #(.width(32)) register_12 (.D(WData), .en(I11), .clk(Clock_in), .Q(B11));  // open: clr
  Register #(.width(32)) register_13 (.D(WData), .en(I12), .clk(Clock_in), .Q(B12));  // open: clr
  Register #(.width(32)) register_14 (.D(WData), .en(I13), .clk(Clock_in), .Q(B13));  // open: clr
  Register #(.width(32)) register_15 (.D(WData), .en(I14), .clk(Clock_in), .Q(B14));  // open: clr
  Register #(.width(32)) register_16 (.D(WData), .en(I15), .clk(Clock_in), .Q(B15));  // open: clr
  Register #(.width(32)) register_17 (.D(WData), .en(I16), .clk(Clock_in), .Q(B16));  // open: clr
  Register #(.width(32)) register_18 (.D(WData), .en(I17), .clk(Clock_in), .Q(B17));  // open: clr
  Register #(.width(32)) register_19 (.D(WData), .en(I18), .clk(Clock_in), .Q(B18));  // open: clr
  Register #(.width(32)) register_20 (.D(WData), .en(I19), .clk(Clock_in), .Q(B19));  // open: clr
  Register #(.width(32)) register_21 (.D(WData), .en(I20), .clk(Clock_in), .Q(B20));  // open: clr
  Register #(.width(32)) register_22 (.D(WData), .en(I21), .clk(Clock_in), .Q(B21));  // open: clr
  Register #(.width(32)) register_23 (.D(WData), .en(I22), .clk(Clock_in), .Q(B22));  // open: clr
  Register #(.width(32)) register_24 (.D(WData), .en(I23), .clk(Clock_in), .Q(B23));  // open: clr
  Register #(.width(32)) register_25 (.D(WData), .en(I24), .clk(Clock_in), .Q(B24));  // open: clr
  Register #(.width(32)) register_26 (.D(WData), .en(I25), .clk(Clock_in), .Q(B25));  // open: clr
  Register #(.width(32)) register_27 (.D(WData), .en(I26), .clk(Clock_in), .Q(B26));  // open: clr
  Register #(.width(32)) register_28 (.D(WData), .en(I27), .clk(Clock_in), .Q(B27));  // open: clr
  Register #(.width(32)) register_29 (.D(WData), .en(I28), .clk(Clock_in), .Q(B28));  // open: clr
  Register #(.width(32)) register_30 (.D(WData), .en(I29), .clk(Clock_in), .Q(B29));  // open: clr
  Register #(.width(32)) register_31 (.D(WData), .en(I30), .clk(Clock_in), .Q(B30));  // open: clr
  Register #(.width(32)) register_32 (.D(WData), .en(I31), .clk(Clock_in), .Q(B31));  // open: clr
  Demultiplexer #(.enable("false"), .select(5)) demultiplexer_1 (
    .out0(I0), .out1(I1), .out2(I2), .out3(I3), .out4(I4), .out5(I5), .out6(I6), .out7(I7), .out8(I8),
    .out9(I9), .out10(I10), .out11(I11), .out12(I12), .out13(I13), .out14(I14), .out15(I15), .out16(I16),
    .out17(I17), .out18(I18), .out19(I19), .out20(I20), .out21(I21), .out22(I22), .out23(I23), .out24(I24),
    .out25(I25), .out26(I26), .out27(I27), .out28(I28), .out29(I29), .out30(I30), .out31(I31), .in(Write),
    .sel(WReg));
  Multiplexer #(.enable("false"), .select(5), .width(32)) multiplexer_1 (
    .in0(B0), .in1(B1), .in2(B2), .in3(B3), .in4(B4), .in5(B5), .in6(B6), .in7(B7), .in8(B8), .in9(B9),
    .in10(B10), .in11(B11), .in12(B12), .in13(B13), .in14(B14), .in15(B15), .in16(B16), .in17(B17),
    .in18(B18), .in19(B19), .in20(B20), .in21(B21), .in22(B22), .in23(B23), .in24(B24), .in25(B25),
    .in26(B26), .in27(B27), .in28(B28), .in29(B29), .in30(B30), .in31(B31), .out(RData1), .sel(RReg1));
  Multiplexer #(.enable("false"), .select(5), .width(32)) multiplexer_2 (
    .in0(B0), .in1(B1), .in2(B2), .in3(B3), .in4(B4), .in5(B5), .in6(B6), .in7(B7), .in8(B8), .in9(B9),
    .in10(B10), .in11(B11), .in12(B12), .in13(B13), .in14(B14), .in15(B15), .in16(B16), .in17(B17),
    .in18(B18), .in19(B19), .in20(B20), .in21(B21), .in22(B22), .in23(B23), .in24(B24), .in25(B25),
    .in26(B26), .in27(B27), .in28(B28), .in29(B29), .in30(B30), .in31(B31), .out(RData2), .sel(RReg2));
endmodule

module Datapath (
  input  [31:0] Instruction
);

  wire alu_ctrl_1_alu_src, clock_1_out;
  wire [3:0] alu_ctrl_1_alu_ctrl0;
  wire [31:0] bit_extender_1_out, multiplexer_1_out, thirtytwo_bit_alu_1_result,
       thirtytwo_register_file_1_rdata1, thirtytwo_register_file_1_rdata2;

  Clock clock_1 (.out(clock_1_out));
  assign bit_extender_1_out = {{20{Instruction[31]}}, Instruction[31:20]};  // Bit_Extender bit_extender_1
  thirtytwo_register_file thirtytwo_register_file_1 (
    .Clock_in(clock_1_out), .Write(1'b1), .WReg(Instruction[11:7]), .WData(thirtytwo_bit_alu_1_result),
    .RReg1(Instruction[19:15]), .RReg2(Instruction[24:20]), .RData1(thirtytwo_register_file_1_rdata1),
    .RData2(thirtytwo_register_file_1_rdata2));
  Multiplexer #(.enable("false"), .width(32)) multiplexer_1 (
    .in0(thirtytwo_register_file_1_rdata2), .in1(bit_extender_1_out), .out(multiplexer_1_out),
    .sel(alu_ctrl_1_alu_src));
  ALU_Ctrl alu_ctrl_1 (
    .I30(Instruction[30]), .I14(Instruction[14]), .I13(Instruction[13]), .I12(Instruction[12]),
    .I6(Instruction[6]), .I5(Instruction[5]), .I4(Instruction[4]), .ALU_Ctrl3(alu_ctrl_1_alu_ctrl0[3]),
    .ALU_Ctrl2(alu_ctrl_1_alu_ctrl0[2]), .ALU_Ctrl1(alu_ctrl_1_alu_ctrl0[1]),
    .ALU_Ctrl0(alu_ctrl_1_alu_ctrl0[0]), .ALU_Src(alu_ctrl_1_alu_src));
  thirtytwo_bit_ALU thirtytwo_bit_alu_1 (
    .ALU_Ctrl(alu_ctrl_1_alu_ctrl0), .A(thirtytwo_register_file_1_rdata1), .B(multiplexer_1_out),
    .Result(thirtytwo_bit_alu_1_result));  // open: C_out
endmodule

module Control (
  input  [6:0] I6_0,
  output MemtoReg,
  output RegWrite,
  output MemRead,
  output MemWrite,
  output Branch
);

  wire not_1_out, not_2_out, not_3_out;

  not not_1 (not_1_out, I6_0[4]);
  not not_2 (not_2_out, I6_0[5]);
  not not_3 (not_3_out, I6_0[6]);
  and and_1 (MemtoReg, not_1_out, not_1_out);
  or or_1 (RegWrite, not_2_out, I6_0[4]);
  and and_2 (MemRead, not_2_out, not_1_out);
  and and_3 (MemWrite, not_3_out, not_1_out);

  assign Branch = I6_0[6];
endmodule

module InstructionMemory (
  input  [23:0] Address,
  input  ClockIn,
  output [31:0] Instruction
);

  wire not_1_out;

  not not_1 (not_1_out, ClockIn);
  RAM #(.addrWidth(22), .asyncread("true"), .dataWidth(32)) ram_1 (
    .addr(Address[23:2]), .we(1'b0), .oe(not_1_out), .dout(Instruction));  // open: clk, din
endmodule

module DRAM64Mx32Bit (
  input  [25:0] Address,
  input  WriteEnable,
  input  OutputEnable,
  input  [31:0] DataIn,
  input  Clock,
  output [31:0] DataOut
);

  wire decoder_1_out0, decoder_1_out1, decoder_1_out2, decoder_1_out3, decoder_2_out0, decoder_2_out1,
       decoder_2_out2, decoder_2_out3;
  wire [31:0] ram_1_dout, ram_2_dout, ram_3_dout, ram_4_dout;

  Decoder #(.select(2)) decoder_1 (
    .out0(decoder_1_out0), .out1(decoder_1_out1), .out2(decoder_1_out2), .out3(decoder_1_out3),
    .sel(Address[25:24]), .en(WriteEnable));
  Decoder #(.select(2)) decoder_2 (
    .out0(decoder_2_out0), .out1(decoder_2_out1), .out2(decoder_2_out2), .out3(decoder_2_out3),
    .sel(Address[25:24]), .en(OutputEnable));
  RAM #(.addrWidth(24), .asyncread("true"), .dataWidth(32)) ram_1 (
    .addr(Address[23:0]), .we(decoder_1_out0), .oe(decoder_2_out0), .clk(Clock), .din(DataIn),
    .dout(ram_1_dout));
  RAM #(.addrWidth(24), .asyncread("true"), .dataWidth(32)) ram_2 (
    .addr(Address[23:0]), .we(decoder_1_out1), .oe(decoder_2_out1), .clk(Clock), .din(DataIn),
    .dout(ram_2_dout));
  RAM #(.addrWidth(24), .asyncread("true"), .dataWidth(32)) ram_3 (
    .addr(Address[23:0]), .we(decoder_1_out2), .oe(decoder_2_out2), .clk(Clock), .din(DataIn),
    .dout(ram_3_dout));
  RAM #(.addrWidth(24), .asyncread("true"), .dataWidth(32)) ram_4 (
    .addr(Address[23:0]), .we(decoder_1_out3), .oe(decoder_2_out3), .clk(Clock), .din(DataIn),
    .dout(ram_4_dout));
  Multiplexer #(.enable("false"), .select(2), .width(32)) multiplexer_1 (
    .in0(ram_1_dout), .in1(ram_2_dout), .in2(ram_3_dout), .in3(ram_4_dout), .out(DataOut),
    .sel(Address[25:24]));
endmodule

module Main_Circuit (
);

  wire alu_ctrl_1_alu_src, and_1_out, clock_1_out, comparator_1_eq, control_1_branch, control_1_memread,
       control_1_memtoreg, control_1_memwrite, control_1_regwrite;
  wire [3:0] alu_ctrl_1_alu_ctrl0;
  wire [7:0] register_1_q_2;
  wire [23:0] register_1_q;
  wire [31:0] adder_1_out, adder_2_out, datamemory_1_dataout, immgen_1_imm32, InstructionMemory_instruction,
       multiplexer_1_out, multiplexer_2_out, multiplexer_3_out, thirtytwo_bit_alu_1_result,
       thirtytwo_register_file_1_rdata1, thirtytwo_register_file_1_rdata2;

  Register #(.width(32)) register_1 (
    .D(multiplexer_2_out), .en(1'b1), .clk(clock_1_out), .Q({register_1_q_2, register_1_q}));  // open: clr
  Clock clock_1 (.out(clock_1_out));
  Adder #(.width(32)) adder_1 (.a({register_1_q_2, register_1_q}), .b(32'h4), .out(adder_1_out));  // open: cin, cout
  InstructionMemory InstructionMemory (
    .Address(register_1_q), .ClockIn(clock_1_out), .Instruction(InstructionMemory_instruction));
  Control control_1 (
    .I6_0(InstructionMemory_instruction[6:0]), .MemtoReg(control_1_memtoreg), .RegWrite(control_1_regwrite),
    .MemRead(control_1_memread), .MemWrite(control_1_memwrite), .Branch(control_1_branch));
  thirtytwo_register_file thirtytwo_register_file_1 (
    .Clock_in(clock_1_out), .Write(control_1_regwrite), .WReg(InstructionMemory_instruction[11:7]),
    .WData(multiplexer_3_out), .RReg1(InstructionMemory_instruction[19:15]),
    .RReg2(InstructionMemory_instruction[24:20]), .RData1(thirtytwo_register_file_1_rdata1),
    .RData2(thirtytwo_register_file_1_rdata2));
  ImmGen immgen_1 (.Instruction(InstructionMemory_instruction), .IMM32(immgen_1_imm32));
  ALU_Ctrl alu_ctrl_1 (
    .I30(InstructionMemory_instruction[30]), .I14(InstructionMemory_instruction[14]),
    .I13(InstructionMemory_instruction[13]), .I12(InstructionMemory_instruction[12]),
    .I6(InstructionMemory_instruction[6]), .I5(InstructionMemory_instruction[5]),
    .I4(InstructionMemory_instruction[4]), .ALU_Ctrl3(alu_ctrl_1_alu_ctrl0[3]),
    .ALU_Ctrl2(alu_ctrl_1_alu_ctrl0[2]), .ALU_Ctrl1(alu_ctrl_1_alu_ctrl0[1]),
    .ALU_Ctrl0(alu_ctrl_1_alu_ctrl0[0]), .ALU_Src(alu_ctrl_1_alu_src));
  Multiplexer #(.enable("false"), .width(32)) multiplexer_1 (
    .in0(thirtytwo_register_file_1_rdata2), .in1(immgen_1_imm32), .out(multiplexer_1_out),
    .sel(alu_ctrl_1_alu_src));
  Comparator #(.width(32)) comparator_1 (
    .a(thirtytwo_register_file_1_rdata1), .b(thirtytwo_register_file_1_rdata2), .eq(comparator_1_eq));  // open: gt, lt
  Adder #(.width(32)) adder_2 (
    .a({register_1_q_2, register_1_q}), .b(immgen_1_imm32), .out(adder_2_out));  // open: cin, cout
  thirtytwo_bit_ALU thirtytwo_bit_alu_1 (
    .ALU_Ctrl(alu_ctrl_1_alu_ctrl0), .A(thirtytwo_register_file_1_rdata1), .B(multiplexer_1_out),
    .Result(thirtytwo_bit_alu_1_result));  // open: C_out
  Multiplexer #(.enable("false"), .width(32)) multiplexer_2 (
    .in0(adder_1_out), .in1(adder_2_out), .out(multiplexer_2_out), .sel(and_1_out));
  and and_1 (and_1_out, control_1_branch, comparator_1_eq);
  DataMemory datamemory_1 (
    .Address(thirtytwo_bit_alu_1_result[25:0]), .MemWrite(control_1_memwrite), .MemRead(control_1_memread),
    .ClockIn(clock_1_out), .DataIn(thirtytwo_register_file_1_rdata2), .DataOut(datamemory_1_dataout));
  Multiplexer #(.enable("false"), .width(32)) multiplexer_3 (
    .in0(thirtytwo_bit_alu_1_result), .in1(datamemory_1_dataout), .out(multiplexer_3_out),
    .sel(control_1_memtoreg));
endmodule

module DataMemory (
  input  [25:0] Address,
  input  MemWrite,
  input  MemRead,
  input  ClockIn,
  input  [31:0] DataIn,
  output [31:0] DataOut
);

  RAM #(.addrWidth(24), .asyncread("true"), .dataWidth(32)) ram_1 (
    .addr(Address[25:2]), .we(MemWrite), .oe(MemRead), .clk(ClockIn), .din(DataIn), .dout(DataOut));
endmodule
